# Fritzing sketch Lab_part3 (saved by Fritzing 0.9.3b)
breadboards: 1

parts:
  U2 = 74HC595 SMD [package="SO16 [SMD]"]
  Dot_Matrix1 = LED Dot Matrix 18mm (0.7 INCH)
  U1 = 74HC595 SMD [package="SO16 [SMD]"]
  R1 = Resistor [tolerance=±5% resistance=220 package="0402 [SMD]"]
  R2 = Resistor [tolerance=±5% resistance=220 package="0402 [SMD]"]
  R3 = Resistor [tolerance=±5% resistance=220 package="0603 [SMD]"]
  R4 = Resistor [tolerance=±5% resistance=220 package="0603 [SMD]"]
  R5 = Resistor [tolerance=±5% resistance=220 package="0603 [SMD]"]
  R6 = Resistor [tolerance=±5% resistance=220 package="0603 [SMD]"]
  R7 = Resistor [tolerance=±5% resistance=220 package="0603 [SMD]"]
  Part1 = Arduino Leonardo (Rev3b)

nets:
  N1: U2.Q3, Dot_Matrix1.Column_1
  N2: U2.Q4, Dot_Matrix1.Column_2
  N3: U2.Q5, Dot_Matrix1.Column_3
  N4: U2.Q6, Dot_Matrix1.Column_5
  N5: U2.Q7, Dot_Matrix1.Column_4
  GND: U2.GND, U2.OE, U1.GND, U1.OE, Part1.GND
  VCC: U2.MR, U2.VCC, U1.MR, U1.VCC, Part1.5V
  N6: U2.SH_CP, Part1.D10_PWM/A10
  N7: U2.ST_CP, Part1.D9_PWM/A9
  N8: U2.DS, Part1.D8/A8
  N9: Dot_Matrix1.Row_3, R4.Pin_0
  N10: Dot_Matrix1.Row_5, R3.Pin_0
  N11: Dot_Matrix1.Row_6, R2.Pin_0
  N12: Dot_Matrix1.Row_7, R1.Pin_0
  N13: Dot_Matrix1.Row_4, R7.Pin_0
  N14: Dot_Matrix1.Row_2, R6.Pin_0
  N15: Dot_Matrix1.Row_1, R5.Pin_0
  N16: U1.Q1, R3.Pin_1
  N17: U1.Q2, R2.Pin_1
  N18: U1.Q3, R1.Pin_1
  N19: U1.Q4, R7.Pin_1
  N20: U1.Q5, R4.Pin_1
  N21: U1.Q7, R5.Pin_1
  N22: U1.SH_CP, Part1.D13_PWM
  N23: U1.ST_CP, Part1.D12/A11
  N24: U1.DS, Part1.D11_PWM
