# Fritzing sketch Sketch-1 (saved by Fritzing 0.9.3b)
breadboards: 1

parts:
  LED1 = RGB LED - (4 legs) [package="5 mm [THT]"]
  R1 = Photocell (LDR) [package=THT]
  Part1 = Arduino Leonardo (Rev3b)
  R2 = Resistor [tolerance=±5% resistance=220 package="2010 [SMD]"]
  R3 = Resistor [tolerance=±5% resistance=220 package="0402 [SMD]"]
  R4 = Resistor [tolerance=±5% resistance=220 package="0402 [SMD]"]
  R5 = Resistor [tolerance=±5% resistance=220 package="0402 [SMD]"]

nets:
  N1: LED1.red_cathode, R3.Pin_0
  N2: LED1.common_anode, R1.pin_1, Part1.GND
  N3: LED1.green_cathode, R4.Pin_0
  N4: LED1.blue_cathode, R5.Pin_0
  N5: R1.pin_0, Part1.A0, R2.Pin_0
  N6: Part1.5V, R2.Pin_1
  N7: Part1.D9_PWM/A9, R3.Pin_1
  N8: Part1.D10_PWM/A10, R4.Pin_1
  N9: Part1.D11_PWM, R5.Pin_1
