# Fritzing sketch Sketch-2 (saved by Fritzing 0.9.3b)
breadboards: 1

parts:
  LED1 = RGB LED - (4 legs) [package="5 mm [THT]"]
  Part1 = Arduino Leonardo (Rev3b)
  R3 = Resistor [tolerance=±5% resistance=220 package="0402 [SMD]"]
  R4 = Resistor [tolerance=±5% resistance=220 package="0402 [SMD]"]
  R5 = Resistor [tolerance=±5% resistance=220 package="0402 [SMD]"]
  hc-sr1 = hc-sr04

nets:
  N1: LED1.red_cathode, R3.Pin_0
  GND: LED1.common_anode, Part1.GND, hc-sr1.GND
  N2: LED1.green_cathode, R4.Pin_0
  N3: LED1.blue_cathode, R5.Pin_0
  5V: Part1.5V, hc-sr1.VCC
  N4: Part1.D9_PWM/A9, R3.Pin_1
  N5: Part1.D10_PWM/A10, R4.Pin_1
  N6: Part1.D11_PWM, R5.Pin_1
  N7: Part1.D12/A11, hc-sr1.Echo
  N8: Part1.D13_PWM, hc-sr1.Trig
