# Fritzing sketch Sketch-3 (saved by Fritzing 0.9.3b)
breadboards: 1

parts:
  LED1 = RGB LED - (4 legs) [package="5 mm [THT]"]
  Part1 = Arduino Leonardo (Rev3b)
  R3 = Resistor [tolerance=±5% resistance=220 package="0402 [SMD]"]
  R4 = Resistor [tolerance=±5% resistance=220 package="0402 [SMD]"]
  R5 = Resistor [tolerance=±5% resistance=220 package="0402 [SMD]"]
  RE1 = Rotary Encoder [package=THT]
  R6 = Resistor [tolerance=±5% resistance=220 package="0402 [SMD]"]
  R7 = Resistor [tolerance=±5% resistance=220 package="0402 [SMD]"]
  R8 = Resistor [tolerance=±5% resistance=220 package="0402 [SMD]"]
  R9 = PHOTOCELL [package=photocell-kit]

nets:
  N1: LED1.red_cathode, R3.Pin_0
  N2: LED1.common_anode, Part1.GND, RE1.EncoderPinC, R6.Pin_1, R7.Pin_1, R9.P$2
  N3: LED1.green_cathode, R4.Pin_0
  N4: LED1.blue_cathode, R5.Pin_0
  N5: Part1.D6_PWM/A7, RE1.EncoderPinB, R7.Pin_0
  N6: Part1.D7, RE1.EncoderPinA, R6.Pin_0
  N7: Part1.5V, R8.Pin_0
  N8: Part1.A0, R8.Pin_1, R9.P$1
  N9: Part1.D9_PWM/A9, R3.Pin_1
  N10: Part1.D10_PWM/A10, R4.Pin_1
  N11: Part1.D11_PWM, R5.Pin_1
